// Logisim project proj1-1.circ as structural Verilog: 4 circuits, main circuit Step 1
module Step_1 (
);

  wire clock_1_out, dec_counter_1__0, dec_counter_1__1, dec_counter_1__2, dec_counter_1__3,
       n8421bcd_dec_driver_1_out_5, n8421bcd_dec_driver_1_out_6, n8421bcd_dec_driver_1_out_7,
       n8421bcd_dec_driver_1_out_8, n8421bcd_dec_driver_1_out_9, n8421bcd_dec_driver_1_out_10,
       n8421bcd_dec_driver_1_out_11;

  Clock clock_1 (.out(clock_1_out));
  dec_counter dec_counter_1 (
    .Clock(clock_1_out), ._0(dec_counter_1__0), ._1(dec_counter_1__1), ._2(dec_counter_1__2),
    ._3(dec_counter_1__3));
  _8421bcd_dec_driver u_8421bcd_dec_driver_1 (
    .in_1(dec_counter_1__0), .in_2(dec_counter_1__1), .in_3(dec_counter_1__2), .in_4(dec_counter_1__3),
    .out_5(n8421bcd_dec_driver_1_out_5), .out_6(n8421bcd_dec_driver_1_out_6),
    .out_7(n8421bcd_dec_driver_1_out_7), .out_8(n8421bcd_dec_driver_1_out_8),
    .out_9(n8421bcd_dec_driver_1_out_9), .out_10(n8421bcd_dec_driver_1_out_10),
    .out_11(n8421bcd_dec_driver_1_out_11));
  _7_Segment_Display u_7_segment_display_1 (
    .g(n8421bcd_dec_driver_1_out_8), .f(n8421bcd_dec_driver_1_out_7), .a(n8421bcd_dec_driver_1_out_6),
    .b(n8421bcd_dec_driver_1_out_5), .e(n8421bcd_dec_driver_1_out_9), .d(n8421bcd_dec_driver_1_out_10),
    .c(n8421bcd_dec_driver_1_out_11));  // open: dp
endmodule

module Step_2 (
);

  wire and_1_out, clock_1_out, dec_counter_1__0, dec_counter_1__1, dec_counter_1__2, dec_counter_1__3,
       dec_counter_2__0, dec_counter_2__1, dec_counter_2__2, dec_counter_2__3, n8421bcd_dec_driver_1_out_5,
       n8421bcd_dec_driver_1_out_6, n8421bcd_dec_driver_1_out_7, n8421bcd_dec_driver_1_out_8,
       n8421bcd_dec_driver_1_out_9, n8421bcd_dec_driver_1_out_10, n8421bcd_dec_driver_1_out_11,
       n8421bcd_dec_driver_2_out_5, n8421bcd_dec_driver_2_out_6, n8421bcd_dec_driver_2_out_7,
       n8421bcd_dec_driver_2_out_8, n8421bcd_dec_driver_2_out_9, n8421bcd_dec_driver_2_out_10,
       n8421bcd_dec_driver_2_out_11;

  dec_counter dec_counter_1 (
    .Clock(and_1_out), ._0(dec_counter_1__0), ._1(dec_counter_1__1), ._2(dec_counter_1__2),
    ._3(dec_counter_1__3));
  _8421bcd_dec_driver u_8421bcd_dec_driver_1 (
    .in_1(dec_counter_1__0), .in_2(dec_counter_1__1), .in_3(dec_counter_1__2), .in_4(dec_counter_1__3),
    .out_5(n8421bcd_dec_driver_1_out_5), .out_6(n8421bcd_dec_driver_1_out_6),
    .out_7(n8421bcd_dec_driver_1_out_7), .out_8(n8421bcd_dec_driver_1_out_8),
    .out_9(n8421bcd_dec_driver_1_out_9), .out_10(n8421bcd_dec_driver_1_out_10),
    .out_11(n8421bcd_dec_driver_1_out_11));
  _7_Segment_Display u_7_segment_display_1 (
    .g(n8421bcd_dec_driver_1_out_8), .f(n8421bcd_dec_driver_1_out_7), .a(n8421bcd_dec_driver_1_out_6),
    .b(n8421bcd_dec_driver_1_out_5), .e(n8421bcd_dec_driver_1_out_9), .d(n8421bcd_dec_driver_1_out_10),
    .c(n8421bcd_dec_driver_1_out_11));  // open: dp
  and and_1 (and_1_out, dec_counter_2__3, dec_counter_2__0);
  Clock clock_1 (.out(clock_1_out));
  _7_Segment_Display u_7_segment_display_2 (
    .g(n8421bcd_dec_driver_2_out_8), .f(n8421bcd_dec_driver_2_out_7), .a(n8421bcd_dec_driver_2_out_6),
    .b(n8421bcd_dec_driver_2_out_5), .e(n8421bcd_dec_driver_2_out_9), .d(n8421bcd_dec_driver_2_out_10),
    .c(n8421bcd_dec_driver_2_out_11));  // open: dp
  dec_counter dec_counter_2 (
    .Clock(clock_1_out), ._0(dec_counter_2__0), ._1(dec_counter_2__1), ._2(dec_counter_2__2),
    ._3(dec_counter_2__3));
  _8421bcd_dec_driver u_8421bcd_dec_driver_2 (
    .in_1(dec_counter_2__0), .in_2(dec_counter_2__1), .in_3(dec_counter_2__2), .in_4(dec_counter_2__3),
    .out_5(n8421bcd_dec_driver_2_out_5), .out_6(n8421bcd_dec_driver_2_out_6),
    .out_7(n8421bcd_dec_driver_2_out_7), .out_8(n8421bcd_dec_driver_2_out_8),
    .out_9(n8421bcd_dec_driver_2_out_9), .out_10(n8421bcd_dec_driver_2_out_10),
    .out_11(n8421bcd_dec_driver_2_out_11));
endmodule

module _8421bcd_dec_driver (
  input  in_1,
  input  in_2,
  input  in_3,
  input  in_4,
  output out_5,
  output out_6,
  output out_7,
  output out_8,
  output out_9,
  output out_10,
  output out_11
);

  wire and_1_out, and_2_out, and_3_out, and_4_out, and_5_out, and_6_out, and_7_out, and_8_out, and_9_out,
       and_10_out, and_11_out, and_12_out, and_13_out, and_14_out, not_1_out, not_2_out, not_3_out, not_4_out;

  not not_1 (not_1_out, in_1);
  not not_2 (not_2_out, in_3);
  not not_3 (not_3_out, in_2);
  not not_4 (not_4_out, in_4);
  and and_1 (and_1_out, in_1, in_2);
  and and_2 (and_2_out, not_1_out, not_3_out);
  and and_3 (and_3_out, in_3, in_1);
  and and_4 (and_4_out, not_4_out, not_2_out, not_1_out);
  and and_5 (and_5_out, not_4_out, not_2_out, in_2);
  and and_6 (and_6_out, in_2, not_1_out);
  and and_7 (and_7_out, in_3, not_3_out);
  and and_8 (and_8_out, not_3_out, not_1_out);
  and and_9 (and_9_out, in_2, not_1_out);
  and and_10 (and_10_out, not_2_out, not_3_out, not_1_out);
  and and_11 (and_11_out, in_3, not_3_out, in_1);
  and and_12 (and_12_out, not_4_out, not_2_out, in_2);
  and and_13 (and_13_out, in_2, not_1_out);
  and and_14 (and_14_out, not_2_out, not_3_out, not_1_out);
  or or_1 (out_11, in_3, not_3_out, in_1);
  or or_2 (out_5, and_1_out, and_2_out, not_2_out);
  or or_3 (out_6, and_3_out, and_4_out, in_4, in_2);
  or or_4 (out_8, and_5_out, and_6_out, and_7_out, in_4);
  or or_5 (out_7, and_8_out, in_4, in_3);
  or or_6 (out_9, and_9_out, and_10_out);
  or or_7 (out_10, and_11_out, and_12_out, and_13_out, and_14_out, in_4);
endmodule

module dec_counter (
  input  Clock,
  output _0,
  output _1,
  output _2,
  output _3
);

  wire and_1_out, and_2_out, and_3_out, and_4_out, and_5_out, and_6_out, and_7_out, D1_qn, D2_qn, D3_qn,
       D4_qn, or_1_out, or_2_out, or_3_out;

  and and_1 (and_1_out, _3, D4_qn);
  and and_2 (and_2_out, _2, _1, _0);
  and and_3 (and_3_out, _2, D3_qn);
  and and_4 (and_4_out, _2, D4_qn);
  and and_5 (and_5_out, D2_qn, _1, _0);
  and and_6 (and_6_out, _1, D4_qn);
  and and_7 (and_7_out, D1_qn, D3_qn, _0);
  or or_1 (or_1_out, and_1_out, and_2_out);
  or or_2 (or_2_out, and_3_out, and_4_out, and_5_out);
  or or_3 (or_3_out, and_6_out, and_7_out);
  D_Flip_Flop #(.trigger("falling")) D1 (.clk(Clock), .D(or_1_out), .Q(_3), .Qn(D1_qn));  // open: preset, en, reset
  D_Flip_Flop #(.trigger("falling")) D2 (.clk(Clock), .D(or_2_out), .Q(_2), .Qn(D2_qn));  // open: preset, en, reset
  D_Flip_Flop #(.trigger("falling")) D3 (.clk(Clock), .D(or_3_out), .Q(_1), .Qn(D3_qn));  // open: preset, en, reset
  D_Flip_Flop #(.trigger("falling")) D4 (.clk(Clock), .D(D4_qn), .Q(_0), .Qn(D4_qn));  // open: preset, en, reset
endmodule
