// Logisim project proj_2.circ as structural Verilog: 4 circuits, main circuit Main
module Main (
  input  in_1,
  input  in_2,
  input  in_3,
  input  in_4,
  input  in_5,
  input  in_6,
  input  in_7,
  input  in_8,
  input  in_9
);

  wire adder_1_cout, adder_1_s, adder_2_cout, adder_2_s, adder_3_cout, adder_3_s, adder_4_cout, adder_4_s,
       n8421bcd_dec_driver_1_out_5, n8421bcd_dec_driver_1_out_6, n8421bcd_dec_driver_1_out_7,
       n8421bcd_dec_driver_1_out_8, n8421bcd_dec_driver_1_out_9, n8421bcd_dec_driver_1_out_10,
       n8421bcd_dec_driver_1_out_11, n8421bcd_dec_driver_2_out_5, n8421bcd_dec_driver_2_out_6,
       n8421bcd_dec_driver_2_out_7, n8421bcd_dec_driver_2_out_8, n8421bcd_dec_driver_2_out_9,
       n8421bcd_dec_driver_2_out_10, n8421bcd_dec_driver_2_out_11, n168421bcd_dec_driver_1_out_7,
       n168421bcd_dec_driver_1_out_8, n168421bcd_dec_driver_1_out_9, n168421bcd_dec_driver_1_out_10,
       n168421bcd_dec_driver_1_out_11, n168421bcd_dec_driver_1_out_12, n168421bcd_dec_driver_1_out_13,
       n168421bcd_dec_driver_1_out_14, not_1_out, or_1_out, xor_1_out, xor_2_out, xor_3_out, xor_4_out;

  _7_Segment_Display u_7_segment_display_1 (
    .g(n8421bcd_dec_driver_1_out_8), .f(n8421bcd_dec_driver_1_out_7), .a(n8421bcd_dec_driver_1_out_6),
    .b(n8421bcd_dec_driver_1_out_5), .e(n8421bcd_dec_driver_1_out_9), .d(n8421bcd_dec_driver_1_out_10),
    .c(n8421bcd_dec_driver_1_out_11));  // open: dp
  _8421bcd_dec_driver u_8421bcd_dec_driver_1 (
    .in_1(in_4), .in_2(in_3), .in_3(in_2), .in_4(in_1), .out_5(n8421bcd_dec_driver_1_out_5),
    .out_6(n8421bcd_dec_driver_1_out_6), .out_7(n8421bcd_dec_driver_1_out_7),
    .out_8(n8421bcd_dec_driver_1_out_8), .out_9(n8421bcd_dec_driver_1_out_9),
    .out_10(n8421bcd_dec_driver_1_out_10), .out_11(n8421bcd_dec_driver_1_out_11));
  _8421bcd_dec_driver u_8421bcd_dec_driver_2 (
    .in_1(in_9), .in_2(in_8), .in_3(in_7), .in_4(in_6), .out_5(n8421bcd_dec_driver_2_out_5),
    .out_6(n8421bcd_dec_driver_2_out_6), .out_7(n8421bcd_dec_driver_2_out_7),
    .out_8(n8421bcd_dec_driver_2_out_8), .out_9(n8421bcd_dec_driver_2_out_9),
    .out_10(n8421bcd_dec_driver_2_out_10), .out_11(n8421bcd_dec_driver_2_out_11));
  Adder adder_1 (.S(adder_1_s), .Cout(adder_1_cout), .a(in_4), .b(xor_1_out), .Cin(in_5));
  xor xor_1 (xor_1_out, in_9, in_5);
  xor xor_2 (xor_2_out, in_8, in_5);
  xor xor_3 (xor_3_out, in_7, in_5);
  Adder adder_2 (.S(adder_2_s), .Cout(adder_2_cout), .a(in_3), .b(xor_2_out), .Cin(adder_1_cout));
  Adder adder_3 (.S(adder_3_s), .Cout(adder_3_cout), .a(in_2), .b(xor_3_out), .Cin(adder_2_cout));
  Adder adder_4 (.S(adder_4_s), .Cout(adder_4_cout), .a(in_1), .b(xor_4_out), .Cin(adder_3_cout));
  xor xor_4 (xor_4_out, in_6, in_5);
  _7_Segment_Display u_7_segment_display_2 (
    .g(n8421bcd_dec_driver_2_out_8), .f(n8421bcd_dec_driver_2_out_7), .a(n8421bcd_dec_driver_2_out_6),
    .b(n8421bcd_dec_driver_2_out_5), .e(n8421bcd_dec_driver_2_out_9), .d(n8421bcd_dec_driver_2_out_10),
    .c(n8421bcd_dec_driver_2_out_11));  // open: dp
  _168421bcd_dec_driver u_168421bcd_dec_driver_1 (
    .in_1(in_5), .A(adder_4_cout), .B(adder_4_s), .C(adder_3_s), .D(adder_2_s), .E(adder_1_s),
    .out_7(n168421bcd_dec_driver_1_out_7), .out_8(n168421bcd_dec_driver_1_out_8),
    .out_9(n168421bcd_dec_driver_1_out_9), .out_10(n168421bcd_dec_driver_1_out_10),
    .out_11(n168421bcd_dec_driver_1_out_11), .out_12(n168421bcd_dec_driver_1_out_12),
    .out_13(n168421bcd_dec_driver_1_out_13), .out_14(n168421bcd_dec_driver_1_out_14));
  _7_Segment_Display u_7_segment_display_3 (
    .g(n168421bcd_dec_driver_1_out_13), .f(n168421bcd_dec_driver_1_out_12),
    .a(n168421bcd_dec_driver_1_out_7), .b(n168421bcd_dec_driver_1_out_8), .e(n168421bcd_dec_driver_1_out_11),
    .d(n168421bcd_dec_driver_1_out_10), .c(n168421bcd_dec_driver_1_out_9));  // open: dp
  _7_Segment_Display u_7_segment_display_4 (
    .f(not_1_out), .a(not_1_out), .b(or_1_out), .e(not_1_out), .d(not_1_out), .c(or_1_out));  // open: g, dp
  or or_1 (or_1_out, not_1_out, n168421bcd_dec_driver_1_out_14);
  not not_1 (not_1_out, n168421bcd_dec_driver_1_out_14);

  // Notes on the sheet:
  //   +/-
  //   =
endmodule

module _8421bcd_dec_driver (
  input  in_1,
  input  in_2,
  input  in_3,
  input  in_4,
  output out_5,
  output out_6,
  output out_7,
  output out_8,
  output out_9,
  output out_10,
  output out_11
);

  wire and_1_out, and_2_out, and_3_out, and_4_out, and_5_out, and_6_out, and_7_out, and_8_out, and_9_out,
       and_10_out, and_11_out, and_12_out, and_13_out, and_14_out, not_1_out, not_2_out, not_3_out, not_4_out;

  not not_1 (not_1_out, in_1);
  not not_2 (not_2_out, in_3);
  not not_3 (not_3_out, in_2);
  not not_4 (not_4_out, in_4);
  and and_1 (and_1_out, in_1, in_2);
  and and_2 (and_2_out, not_1_out, not_3_out);
  and and_3 (and_3_out, in_3, in_1);
  and and_4 (and_4_out, not_4_out, not_2_out, not_1_out);
  and and_5 (and_5_out, not_4_out, not_2_out, in_2);
  and and_6 (and_6_out, in_2, not_1_out);
  and and_7 (and_7_out, in_3, not_3_out);
  and and_8 (and_8_out, not_3_out, not_1_out);
  and and_9 (and_9_out, in_2, not_1_out);
  and and_10 (and_10_out, not_2_out, not_3_out, not_1_out);
  and and_11 (and_11_out, in_3, not_3_out, in_1);
  and and_12 (and_12_out, not_4_out, not_2_out, in_2);
  and and_13 (and_13_out, in_2, not_1_out);
  and and_14 (and_14_out, not_2_out, not_3_out, not_1_out);
  or or_1 (out_11, in_3, not_3_out, in_1);
  or or_2 (out_5, and_1_out, and_2_out, not_2_out);
  or or_3 (out_6, and_3_out, and_4_out, in_4, in_2);
  or or_4 (out_8, and_5_out, and_6_out, and_7_out, in_4);
  or or_5 (out_7, and_8_out, in_4, in_3);
  or or_6 (out_9, and_9_out, and_10_out);
  or or_7 (out_10, and_11_out, and_12_out, and_13_out, and_14_out, in_4);
endmodule

module Adder (
  input  a,
  input  b,
  input  Cin,
  output S,
  output Cout
);

  wire and_1_out, and_2_out, and_3_out, and_4_out, and_5_out, and_6_out, and_7_out, not_1_out, not_2_out,
       not_3_out;

  not not_1 (not_1_out, a);
  not not_2 (not_2_out, b);
  not not_3 (not_3_out, Cin);
  and and_1 (and_1_out, not_1_out, not_2_out, Cin);
  and and_2 (and_2_out, not_1_out, b, not_3_out);
  and and_3 (and_3_out, a, b, Cin);
  and and_4 (and_4_out, a, not_2_out, not_3_out);
  and and_5 (and_5_out, a, b);
  and and_6 (and_6_out, b, Cin);
  and and_7 (and_7_out, a, Cin);
  or or_1 (S, and_1_out, and_2_out, and_3_out, and_4_out);
  or or_2 (Cout, and_5_out, and_6_out, and_7_out);
endmodule

module _168421bcd_dec_driver (
  input  in_1,
  input  A,
  input  B,
  input  C,
  input  D,
  input  E,
  output out_7,
  output out_8,
  output out_9,
  output out_10,
  output out_11,
  output out_12,
  output out_13,
  output out_14
);

  wire and_1_out, and_2_out, and_3_out, and_4_out, and_5_out, and_6_out, and_7_out, and_8_out, and_9_out,
       and_10_out, and_11_out, and_12_out, and_13_out, and_14_out, and_15_out, and_16_out, and_17_out,
       and_18_out, and_19_out, and_20_out, and_21_out, and_22_out, and_23_out, and_24_out, and_25_out,
       and_26_out, and_27_out, and_28_out, and_29_out, and_30_out, and_31_out, and_32_out, and_33_out,
       and_34_out, and_35_out, and_36_out, and_37_out, not_1_out, not_2_out, not_3_out, not_4_out, not_5_out,
       xor_1_out;

  xor xor_1 (xor_1_out, in_1, A);
  not not_1 (not_1_out, B);
  not not_2 (not_2_out, xor_1_out);
  not not_3 (not_3_out, D);
  not not_4 (not_4_out, C);
  not not_5 (not_5_out, E);
  and and_1 (and_1_out, not_4_out, not_5_out);
  and and_2 (and_2_out, B, not_3_out);
  and and_3 (and_3_out, C, E);
  and and_4 (and_4_out, not_1_out, D);
  and and_5 (and_5_out, B, not_4_out);
  and and_6 (and_6_out, B, not_3_out);
  and and_7 (and_7_out, B, not_5_out);
  and and_8 (and_8_out, not_2_out, not_3_out, not_5_out);
  and and_9 (and_9_out, not_2_out, not_1_out, not_4_out);
  and and_10 (and_10_out, not_1_out, not_4_out, D);
  and and_11 (and_11_out, not_1_out, not_4_out, E);
  and and_12 (and_12_out, not_1_out, D, E);
  and and_13 (and_13_out, B, not_4_out);
  and and_14 (and_14_out, not_1_out, not_3_out);
  and and_15 (and_15_out, C, D);
  and and_16 (and_16_out, not_4_out, not_5_out);
  and and_17 (and_17_out, B, not_3_out);
  and and_18 (and_18_out, C, not_3_out, E);
  and and_19 (and_19_out, B, C, E);
  and and_20 (and_20_out, not_1_out, not_4_out, D);
  and and_21 (and_21_out, not_1_out, D, not_5_out);
  and and_22 (and_22_out, not_4_out, not_5_out);
  and and_23 (and_23_out, B, not_3_out, not_5_out);
  and and_24 (and_24_out, not_1_out, D, not_5_out);
  and and_25 (and_25_out, C, D);
  and and_26 (and_26_out, B, not_4_out, not_3_out);
  and and_27 (and_27_out, B, D, not_5_out);
  and and_28 (and_28_out, not_1_out, C, not_3_out);
  and and_29 (and_29_out, not_1_out, not_3_out, not_5_out);
  and and_30 (and_30_out, B, C);
  and and_31 (and_31_out, C, not_3_out);
  and and_32 (and_32_out, B, not_3_out);
  and and_33 (and_33_out, C, not_5_out);
  and and_34 (and_34_out, xor_1_out, not_3_out, not_5_out);
  and and_35 (and_35_out, not_1_out, not_4_out, D);
  and and_36 (and_36_out, B, C);
  and and_37 (and_37_out, B, D);
  or or_1 (out_14, xor_1_out, and_36_out, and_37_out);
  or or_2 (out_7, xor_1_out, and_1_out, and_2_out, and_3_out, and_4_out);
  or or_3 (out_8, and_5_out, and_6_out, and_7_out, and_8_out, and_9_out, and_10_out, and_11_out, and_12_out);
  or or_4 (out_9, xor_1_out, E, and_13_out, and_14_out, and_15_out);
  or or_5 (out_10, and_16_out, and_17_out, and_18_out, and_19_out, and_20_out, and_21_out);
  or or_6 (out_11, and_22_out, and_23_out, and_24_out);
  or or_7 (out_12, xor_1_out, and_25_out, and_26_out, and_27_out, and_28_out, and_29_out);
  or or_8 (out_13, and_30_out, and_31_out, and_32_out, and_33_out, and_34_out, and_35_out);
endmodule
